# Fritzing sketch kitchen_watch (saved by Fritzing 0.9.3b)
breadboards: 1

parts:
  U2 = STM32F103 [package=LQFP-48]
  DS1 = DS18B20 1-Wire Temperature Sensor [part_number=DS18B20]
  R1 = Resistor [tolerance=±20% resistance=4.7k package=THT]
  LCD1 = LCD screen
  R2 = Resistor [tolerance=±5% resistance=3.3k package=THT]
  Part1 = Real Time Clock Module - DS1307 RTC Breakout Board
  KB1 = 1*4 Membrane Matrix Keypad
  Q1 = NPN-Transistor [package="SOT-23 [SMD]"]
  R3 = Resistor [tolerance=±20% resistance=1k package=THT]
  R4 = Resistor [tolerance=±20% resistance=1k package=THT]
  J1 = Piezo Speaker

nets:
  N1: U2.PD1-OSC_OUT, LCD1.RS
  N2: U2.VSSA, LCD1.E
  N3: U2.PA3, LCD1.DB4
  N4: U2.PA4, LCD1.DB5
  N5: U2.PA5, LCD1.DB6
  N6: U2.PA6, LCD1.DB7
  VDD: U2.VSS_1, DS1.VDD, R1.Pin_0, LCD1.VDD, Part1.5V, R3.Pin_0, R4.Pin_0, J1.pin2
  GND: U2.VDD_2#23, DS1.GND, LCD1.VSS, LCD1.R/W, R2.Pin_0, Q1.1
  N7: U2.PB12, Part1.GND
  N8: U2.PB13, Part1.SQW
  N9: U2.PB14, Part1.SCL
  N10: U2.PB15, Part1.SDA
  N11: U2.PA13, KB1.pin5
  N12: U2.VSS_2, KB1.pin4
  N13: U2.VDD_2#35, KB1.pin3
  N14: U2.PA14, KB1.pin2
  N15: U2.PA15, KB1.pin1
  N16: U2.PB8, Q1.0, R3.Pin_1
  N17: U2.PB9, DS1.DQ, R1.Pin_1
  N18: LCD1.V0, R2.Pin_1
  N19: Q1.2, R4.Pin_1, J1.pin1

custom parts:
  1*4 Membrane Matrix Keypad: Membrane Matrix 1x4 Keypad
